// Logisim project clock_assignment.circ as structural Verilog: 1 circuit, main circuit main
module main (
);

  wire button_1_out, clock_1_out, counter_1_carry;
  wire [3:0] counter_1_q, counter_2_q;

  Clock clock_1 (.out(clock_1_out));
  Counter #(.max('h9), .width(4)) counter_1 (
    .clr(button_1_out), .clk(clock_1_out), .carry(counter_1_carry), .Q(counter_1_q));  // open: load, up, count, D
  Hex_Digit_Display hex_digit_display_1 (.value(counter_2_q));  // open: dp
  Hex_Digit_Display hex_digit_display_2 (.value(counter_1_q));  // open: dp
  Counter #(.max('h5), .width(4)) counter_2 (
    .clr(button_1_out), .count(counter_1_carry), .clk(clock_1_out), .Q(counter_2_q));  // open: load, up, D, carry
  Button button_1 (.out(button_1_out));

  // Notes on the sheet:
  //   Please note this is the correct way to chain counters together 
  //   Push to Reset
endmodule
